# Fritzing sketch printer (saved by Fritzing 0.7.4b)
breadboards: 1

parts:
  Arduino_Ethernet_Shield1 = Arduino Ethernet Shield
  Ready_LED = LED - 5mm [color="Green (570nm)" package="5 mm [THT]"]
  Downloading_LED = LED - 5mm [color="Yellow (595nm)" package="5 mm [THT]"]
  Error_LED = LED - 5mm [color="Red (633nm)" package="5 mm [THT]"]
  R1 = Resistor [tolerance=±5% resistance=10k package=THT]
  J1 = male pin header, 3 pins [form="♂ (male)"]
  J2 = male pin header, 2 pins [form="♂ (male)"]
  Power_plug1 = Power plug
  S1 = Pushbutton [package="[THT]"]
  R2 = Resistor [tolerance=±5% resistance=220 package=THT]

nets:
  GND: Arduino_Ethernet_Shield1.GND, R1.Pin_1, J1.pin3, J2.pin2, Power_plug1.GND, R2.Pin_1
  N1: Arduino_Ethernet_Shield1.D9, J1.pin2
  N2: Arduino_Ethernet_Shield1.D8, J1.pin1
  N3: Arduino_Ethernet_Shield1.D7, Error_LED.anode
  N4: Arduino_Ethernet_Shield1.D6, Downloading_LED.anode
  N5: Arduino_Ethernet_Shield1.D5, Ready_LED.anode
  N6: Arduino_Ethernet_Shield1.D3, S1.Pin_1, S1.Pin_2, R2.Pin_0
  N7: Arduino_Ethernet_Shield1.+5V, S1.Pin_3, S1.Pin_4
  VIN: Arduino_Ethernet_Shield1.VIN, J2.pin1, Power_plug1.VCC
  N8: Ready_LED.cathode, Downloading_LED.cathode, Error_LED.cathode, R1.Pin_0
